# Fritzing sketch circuit (saved by Fritzing 0.9.3b)
breadboards: 1

parts:
  Bat1 = battery_holder_single_18650
  Bat2 = battery_holder_single_18650
  U1 = NodeMCU V1.0
  D1 = Rectifier Diode [part_number=1N4001 package="300 mil [THT]"]
  C1 = Electrolytic Capacitor [capacitance=0.22µF voltage=16V package="100 mil [THT, electrolytic]"]
  C2 = Electrolytic Capacitor [capacitance=22µF voltage=16V package="100 mil [THT, electrolytic]"]
  U1_2 = V_REG_LD1117VXX [part_number=LD1117V33 package=78xxl]
  S1 = Pushbutton [package="[THT]"]
  S2 = Pushbutton [package="[THT]"]
  S3 = Pushbutton [package="[THT]"]
  R1 = Resistor [tolerance=±5% resistance=10k package=THT]
  R2 = Resistor [tolerance=±5% resistance=10k package=THT]
  R3 = Resistor [tolerance=±5% resistance=10k package=THT]
  VL53L0X1 = VL53L0X ToF laser distance sensor [package=THT]
  LSM6DSOX1 = Adafruit_LSM6DSOX
  S4 = 0.91 inch OLED I2C Display 128 x 32 Pixels

nets:
  N1: Bat1.+#0, Bat2.+#1
  N2: Bat1.+#1, D1.anode
  GND: Bat2.+#0, U1.GND, C1.-, C2.-, U1_2.GND, R1.Pin_1, R2.Pin_1, R3.Pin_1, VL53L0X1.GND, LSM6DSOX1.GND, S4.GND
  N3: U1.D1, VL53L0X1.SCL, LSM6DSOX1.SCL, S4.SCL
  N4: U1.D2, VL53L0X1.SDA, LSM6DSOX1.SDA, S4.SDA
  N5: U1.D5, S1.Pin_1, S1.Pin_2, R2.Pin_0
  N6: U1.D6, S2.Pin_1, S2.Pin_2, R3.Pin_0
  N7: U1.D7, S3.Pin_1, S3.Pin_2, R1.Pin_0
  VCC: U1.3V3, C2.+, U1_2.OUT, S1.Pin_3, S1.Pin_4, S2.Pin_3, S2.Pin_4, S3.Pin_3, S3.Pin_4, VL53L0X1.VIN, LSM6DSOX1.VCC, S4.VCC
  N8: D1.cathode, C1.+, U1_2.IN

custom parts:
  battery_holder_single_18650: single 18650 battery holder
  NodeMCU V1.0: ESP8266 based NodeMCU
  VL53L0X ToF laser distance sensor: Time of Flight laser distance sensor VL53L0X.
