# Fritzing sketch Untitled Sketch (saved by Fritzing 0.9.3b)
breadboards: 1

parts:
  U1 = NodeMCU V1.0
  S1 = Pushbutton [package="[THT]"]
  S2 = Pushbutton [package="[THT]"]
  S3 = Pushbutton [package="[THT]"]

nets:
  N1: U1.D5, S3.Pin_1, S3.Pin_2
  N2: U1.D6, S2.Pin_1, S2.Pin_2
  N3: U1.D7, S1.Pin_1, S1.Pin_2
  N4: U1.GND, S1.Pin_3, S1.Pin_4, S2.Pin_3, S2.Pin_4, S3.Pin_3, S3.Pin_4

custom parts:
  NodeMCU V1.0: ESP8266 based NodeMCU
